# Fritzing sketch esp_temp_sensor (saved by Fritzing 0.9.3b)
breadboards: 1

parts:
  VCC1 = Battery block 9V
  U1 = ESP8266 WiFi Module [part_number=ESP8266]
  U2 = V_REG_LD1117VXX [package=78xxl]
  C2 = Capacitor Polarized [package=cpol-radial-100uf-25v]
  C1 = Capacitor Polarized [package=cpol-radial-100uf-25v]
  DHT1 = DHT11 Humitidy and Temperature Sensor (3 pins)

nets (from the schematic view):
  GND: VCC1.-, U1.GND, U2.GND, C2.-, C1.-, DHT1.GND
  N1: VCC1.+, U2.IN, C1.+, DHT1.VDD
  N2: U1.VCC, U2.OUT, C2.+
  N3: U1.GPIO_0, DHT1.DATA

custom parts:
  ESP8266 WiFi Module: Generic WiFi Module based on the ESP8266 with onboard PCB antenna and UART communications
  DHT11 Humitidy and Temperature Sensor (3 pins): DHT11 Humidity and Temperature Sensor (3 pins) from the design created by John De Cristofaro for Adafruit Industries.
