# Fritzing sketch esp_motion_sensor (saved by Fritzing 0.9.3b)
breadboards: 1

parts:
  VCC1 = Battery block 9V
  U1 = ESP8266 WiFi Module [part_number=ESP8266]
  U2 = V_REG_LD1117VXX [package=78xxl]
  C2 = Capacitor Polarized [package=cpol-radial-100uf-25v]
  PIR1 = PIR sensor
  PIR2 = PIR sensor
  C1 = Capacitor Polarized [package=cpol-radial-100uf-25v]

nets:
  GND: VCC1.-, U1.GND, U2.GND, C2.-, PIR1.GND, PIR2.GND, C1.-
  N1: VCC1.+, U2.IN, C1.+
  VDD: U1.VCC, U1.CH_PD, U2.OUT, C2.+, PIR1.VDD, PIR2.VDD
  N2: U1.GPIO_0, PIR2.SIG
  N3: U1.GPIO_2, PIR1.SIG

custom parts:
  ESP8266 WiFi Module: Generic WiFi Module based on the ESP8266 with onboard PCB antenna and UART communications
